// Logisim project Controller.circ as structural Verilog: 1 circuit, main circuit Control Store
module Control_Store (
  input  [7:0] Instruction,
  output out_2,
  output out_3,
  output out_4,
  output out_5,
  output out_6,
  output out_7
);

  wire and_1_out, and_2_out, and_3_out, and_4_out, and_5_out, and_6_out, and_7_out, and_8_out, and_9_out,
       and_10_out, and_11_out, not_1_out, not_2_out, not_3_out, not_4_out;

  not not_1 (not_1_out, Instruction[7]);
  not not_2 (not_2_out, Instruction[6]);
  not not_3 (not_3_out, Instruction[5]);
  not not_4 (not_4_out, Instruction[4]);
  and and_1 (and_1_out, not_1_out, not_2_out);
  and and_2 (and_2_out, not_2_out, Instruction[4]);
  or or_1 (out_2, and_1_out, and_2_out, and_3_out);
  and and_3 (and_3_out, Instruction[5], not_4_out);
  or or_2 (out_3, not_2_out, Instruction[5], Instruction[4]);
  or or_3 (out_4, Instruction[7], Instruction[6], Instruction[5], not_4_out);
  and and_4 (and_4_out, not_1_out, not_3_out, Instruction[4]);
  and and_5 (and_5_out, Instruction[6], not_3_out);
  or or_4 (out_5, and_4_out, and_5_out, and_6_out);
  and and_6 (and_6_out, not_2_out, Instruction[5]);
  and and_7 (and_7_out, not_2_out, Instruction[4]);
  or or_5 (out_6, and_7_out, and_8_out);
  and and_8 (and_8_out, Instruction[7], not_2_out, not_3_out);
  and and_9 (and_9_out, not_1_out, not_2_out, Instruction[5], not_4_out);
  and and_10 (and_10_out, not_2_out, Instruction[5], Instruction[4]);
  or or_6 (out_7, and_9_out, and_10_out, and_11_out);
  and and_11 (and_11_out, Instruction[7], not_2_out, Instruction[4]);

  // Notes on the sheet:
  //   A
  //   B
  //   C
  //   D
  //   F0
  //   F1
  //   ENA
  //   ENB
  //   INVA
  //   INC
endmodule
